# Fritzing sketch wiring (saved by Fritzing 0.9.6b)
breadboards: 1

parts:
  Mod1 = Raspberry Pi 4B
  Part1 = Logic Level Converter
  NEOPIXEL1 = Neopixel Strip -- White (60/m) [part_number=1138]
  JACK1 = 2.1mm Barrel Jack with Terminal Block  # not connected

nets:
  N1: Mod1.3V3, Part1.LV
  N2: Mod1.5V, Part1.HV
  GND: Mod1.GND, Part1.GND, NEOPIXEL1.GND
  N3: Mod1.GPIO18, Part1.TX_LV
  N4: Part1.TX_HV, NEOPIXEL1.DI

custom parts:
  Neopixel Strip -- White (60/m): Neopixel Strip, White, 60 pixels per meter.
